// Logisim project Single_cycle_block.circ as structural Verilog: 1 circuit, main circuit main
module main (
  output [31:0] out_1,
  output [31:0] out_2,
  output [31:0] out_3,
  output [31:0] out_4,
  output [31:0] out_5,
  output [31:0] out_6,
  output [31:0] out_7,
  output [31:0] out_8,
  output [31:0] out_9,
  output [31:0] out_10,
  output [31:0] out_11,
  output [31:0] out_12,
  output [31:0] out_13,
  output [31:0] out_14,
  output [31:0] out_15,
  output [31:0] out_16,
  output [31:0] out_17,
  output [31:0] out_18,
  output [31:0] out_19,
  output [31:0] out_20,
  output [31:0] out_21,
  output [31:0] out_22,
  output [31:0] out_23,
  output [31:0] out_24,
  output [31:0] out_25,
  output [31:0] out_26,
  output [31:0] out_27,
  output [31:0] out_28,
  output [31:0] out_29,
  output [31:0] out_30,
  output [31:0] out_31,
  output [31:0] out_32
);

  wire clock_1_out, EXT_OP, Kill_1, Kill_2, less_falg, less_Unsign_falg, main_2_out_2, MEM_Read, MEM_Read_EX,
       MEM_Read_mem, MEM_Write, MEM_Write_EX, MEM_Write_mem, or_1_out, Reg_write, Reg_write_EX,
       reg_write_mem, reg_write_WB, SSET, Stall, WB, WB_EX, WB_mem, Zero_flag;
  wire [1:0] ALU_SRC, ALU_SRC_EX, Forwad_B, Forward_A, PC_SELC, Rd_SRC, Rd_SRC_EX, rd_src_mem, rd_src_WB;
  wire [3:0] func_4bit;
  wire [4:0] immd_L, immd_L_ex, multiplexer_1_out, opcode_branch, RD_EX, rd_mem, rd_WB, Rs_EX, Rs_ID, Rt_EX,
       Rt_ID;
  wire [5:0] opcode;
  wire [9:0] ALU_OP, ALU_OP_EX;
  wire [10:0] immd_U_ex;
  wire [15:0] imm16, imm16_16bit_EX, imm16_16bit_mem, imm16_16bit_wb;
  wire [19:0] PC, PC_EX, PC_ID, PC_Plus_1, PC_Plus_1_EX, PC_Plus_1_ID, pc_plus_1_mem, PC_plus_1_WB;
  wire [31:0] alu_res, ALU_res_EX, Alu_res_mem, bit_extender_2_out, bit_extender_3_out, bit_extender_4_out,
       BusA_ID, BUSB_EX, BusB_ID, BUSB_mem, BUSB_wb, imm16_32_mem, imm16_32_wb, immdL_immdU_EX,
       main_4_instruction, main_8_p20, main_10_data_out, mem_2prev, multiplexer_2_out, multiplexer_4_out,
       multiplexer_5_out, multiplexer_6_out, multiplexer_7_out, WB_3Prev;
  wire [31:16] imm16_32_EX;

  // Probe on out_1
  // Probe on out_15
  // Probe on out_29
  Clock clock_1 (.out(clock_1_out));
  // Probe on PC_SELC
  // Probe on out_2
  // Probe on out_16
  // Probe on out_30
  // Probe on out_3
  // Probe on out_17
  // Probe on out_31
  // Probe on PC
  // Probe on opcode
  // Probe on out_4
  // Probe on out_18
  // Probe on out_32
  // pc_new_main main_1: pin names not known; wires that end beside it: {imm16[15:9], func_4bit, imm16[4:0]}, BusA_ID, immd_U_ex, immd_L_ex, PC_EX, Stall, PC_SELC, clock_1_out, PC, PC_Plus_1
  // Probe on out_5
  // Probe on out_19
  // Probe on opcode_branch
  // Probe on out_6
  // Probe on out_7
  // Probe on out_20
  // Probe on opcode_branch
  is_branch_main main_2 (.in_1(opcode_branch), .out_2(main_2_out_2));
  // Probe on out_21
  // Probe on Zero_flag
  Multiplexer #(.width(5), .enable("false")) multiplexer_1 (
    .in0(opcode[4:0]), .in1(opcode_branch), .out(multiplexer_1_out), .sel(main_2_out_2));
  // Probe on PC
  // Probe on out_8
  // Probe on out_22
  // Probe on out_9
  // Probe on out_23
  PC_Control_Unit_main main_3 (
    .in_1(Zero_flag), .in_2(less_falg), .in_3(less_Unsign_falg), .op_code_5bit(multiplexer_1_out),
    .out_6(PC_SELC), .Kill_1(Kill_1), .Kill_2(Kill_2));
  // Probe on out_10
  // Probe on out_24
  // Probe on out_11
  // Probe on out_25
  // Probe on out_12
  // Probe on out_26
  or or_1 (or_1_out, Stall, Kill_2);
  // Probe on out_13
  // Probe on out_27
  // Probe on out_14
  // Probe on out_28
  main_control_unit main_control_unit_1 (
    .opcode(opcode), .reg_write(Reg_write), .ext_op(EXT_OP), .Rd_src(Rd_SRC), .alu_src(ALU_SRC),
    .mem_write(MEM_Read), .mem_read(MEM_Write), .wb(WB), .Stall(or_1_out), .out_10(SSET));
  Instruction_Mem_main main_4 (.Address(PC), .Instruction(main_4_instruction));
  // Probe on ALU_SRC
  // Probe on main_4_instruction
  Multiplexer #(.width(32), .enable("false")) multiplexer_2 (
    .in0(main_4_instruction), .in1({32{1'b0}}), .out(multiplexer_2_out), .sel(Kill_2));
  // Probe on Rd_SRC
  // Probe on multiplexer_2_out
  // Probe on PC_Plus_1_ID
  if_id_main main_5 (
    .Instruction(multiplexer_2_out), .PC_plus_1(PC_Plus_1),
    .out_6({imm16[15:9], func_4bit, imm16[4:0], Rs_ID, immd_L, opcode}), .out_7(PC_Plus_1_ID),
    .in_5(clock_1_out), .stall(Stall), .PC(PC), .out_8(PC_ID));
  // Probe on {imm16[15:9], func_4bit, imm16[4:0], Rs_ID, immd_L, opcode}
  Register #(.width(5)) register_1 (.D(opcode[4:0]), .en(1'b1), .clk(clock_1_out), .Q(opcode_branch));  // open: clr
  // Probe on opcode_branch
  assign immdL_immdU_EX = {{16{immd_U_ex[10]}}, {immd_U_ex, immd_L_ex}};  // Bit_Extender bit_extender_1
  // Probe on immd_L
  // Probe on immd_L
  assign bit_extender_2_out = {{16{imm16[15]}}, {imm16[15:9], func_4bit, imm16[4:0]}};  // Bit_Extender bit_extender_2
  assign bit_extender_3_out = {{16{1'b0}}, {imm16[15:9], func_4bit, imm16[4:0]}};  // Bit_Extender bit_extender_3
  Multiplexer #(.width(5), .enable("false")) multiplexer_3 (.in0(imm16[4:0]), .in1(immd_L), .out(Rt_ID), .sel(SSET));
  // Probe on rd_WB
  // Probe on SSET
  Forward_main main_6 (
    .Reg_Wr_EX(Reg_write_EX), .Reg_Wr_MEM(reg_write_mem), .Reg_Wr_WB(reg_write_WB), .Rs(Rs_ID), .Rt(Rt_ID),
    .Forwad_A(Forward_A), .Rd_EX(RD_EX), .Rd_MEM(rd_mem), .Rd_WB(rd_WB), .Stall(Stall),
    .MEM_Read_EX(MEM_Read_EX), .Forwad_B(Forwad_B));
  Multiplexer #(.width(32), .enable("false")) multiplexer_4 (
    .in0(bit_extender_2_out), .in1(bit_extender_3_out), .out(multiplexer_4_out), .sel(EXT_OP));
  // Probe on Forward_A
  // Probe on Stall
  // Probe on multiplexer_4_out
  // Probe on reg_write_WB
  // Probe on Forwad_B
  regfile_new_main main_7 (
    .Ra(Rs_ID), .Rb(Rt_ID), .Rw(rd_WB), .Reg_write(reg_write_WB), .Bus_W(WB_3Prev), .Bus_A(BusA_ID),
    .Bus_B(BusB_ID), .Clk(clock_1_out), .R1(out_2), .R2(out_3), .R3(out_4), .R4(out_5), .R0(out_1),
    .R5(out_6), .R6(out_7), .R7(out_8), .R8(out_9), .R9(out_10), .R10(out_11), .R11(out_12), .R12(out_13),
    .R13(out_14), .R14(out_15), .R15(out_16), .R16(out_17), .R17(out_18), .R18(out_19), .R19(out_20),
    .R20(out_21), .R21(out_22), .R22(out_23), .R23(out_24), .R24(out_25), .R25(out_26), .R26(out_27),
    .R27(out_28), .R28(out_29), .R29(out_30), .R30(out_31), .R31(out_32));
  // Probe on BusB_ID
  block1 block1_1 (.op_code(opcode), .ALU_OP(ALU_OP), .func(func_4bit));
  // Probe on ALU_OP
  Multiplexer #(.select(2), .width(32), .enable("false")) multiplexer_5 (
    .in0(BusA_ID), .in1(ALU_res_EX), .in2(mem_2prev), .in3(WB_3Prev), .out(multiplexer_5_out), .sel(Forward_A));
  Multiplexer #(.select(2), .width(32), .enable("false")) multiplexer_6 (
    .in0(BusB_ID), .in1(ALU_res_EX), .in2(mem_2prev), .in3(WB_3Prev), .out(multiplexer_6_out), .sel(Forwad_B));
  // Probe on multiplexer_5_out
  // Probe on multiplexer_6_out
  // Probe on immd_L
  // Probe on ALU_SRC
  // id_ex_main main_8: pin names not known; wires that end beside it: multiplexer_4_out, immd_L, {imm16[15:9], func_4bit}, multiplexer_5_out, multiplexer_6_out, Rs_ID, Rt_ID, PC_Plus_1_ID, MEM_Read, MEM_Write, WB, Reg_write, Rd_SRC, immd_L, ALU_OP, ALU_SRC, {imm16_32_EX, imm16_16bit_EX}, immd_L_ex, immd_U_ex, main_8_p20, BUSB_EX, Rs_EX, Rt_EX, PC_Plus_1_EX, MEM_Read_EX, MEM_Write_EX, WB_EX, Reg_write_EX, Rd_SRC_EX, RD_EX, ALU_OP_EX, ALU_SRC_EX
  // Probe on ALU_SRC_EX
  // Probe on RD_EX
  // Probe on ALU_SRC_EX
  // Probe on {imm16_32_EX, imm16_16bit_EX}
  // Probe on BUSB_EX
  // Probe on main_8_p20
  Multiplexer #(.select(2), .width(32), .enable("false")) multiplexer_7 (
    .in0({imm16_32_EX, imm16_16bit_EX}), .in1(BUSB_EX), .in2(immdL_immdU_EX), .out(multiplexer_7_out),
    .sel(ALU_SRC_EX));  // open: in3
  // Probe on multiplexer_7_out
  ALU alu_1 (
    .ALU_Result(alu_res), .less_flag_unsign(less_falg), .less_flag(less_Unsign_falg), .Zero_flag(Zero_flag),
    .A(main_8_p20), .B(multiplexer_7_out), .ALU_Opration(ALU_OP_EX));  // open: Overflow
  assign bit_extender_4_out = {{12{PC_Plus_1_EX[19]}}, PC_Plus_1_EX};  // Bit_Extender bit_extender_4
  // Probe on bit_extender_4_out
  // Probe on ALU_res_EX
  Multiplexer #(.select(2), .width(32), .enable("false")) multiplexer_8 (
    .in0({BUSB_EX[15:0], imm16_16bit_EX}), .in1({imm16_32_EX, imm16_16bit_EX}), .in2(alu_res),
    .in3(bit_extender_4_out), .out(ALU_res_EX), .sel(Rd_SRC_EX));
  // Probe on Rd_SRC_EX
  // Probe on RD_EX
  ex_mem_main main_9 (
    .in_1(clock_1_out), .WB(WB_EX), .MEM_Read(MEM_Read_EX), .MEM_Write(MEM_Write_EX),
    .Reg_write(Reg_write_EX), .Rd_src(Rd_SRC_EX), .PC_plus_1(PC_Plus_1_EX), .Rd(RD_EX), .Alu_res(ALU_res_EX),
    .out_17(WB_mem), .out_18(MEM_Read_mem), .out_19(MEM_Write_mem), .out_20(reg_write_mem),
    .out_21(rd_src_mem), .out_22(pc_plus_1_mem), .out_23(rd_mem), .out_24(Alu_res_mem),
    .imm16_16bit_EX(imm16_16bit_EX), .out_25(imm16_16bit_mem), .imm16_32_EX({imm16_32_EX, imm16_16bit_EX}),
    .out_26(imm16_32_mem), .BUSB_EX(BUSB_EX), .out_27(BUSB_mem));  // open: SSET, out_28, zero_flag, out_29, Less_flag, out_30, less_flag_unsign, out_31
  // Probe on rd_mem
  // Probe on BUSB_mem
  Data_Mem_main main_10 (
    .Mem_Write(MEM_Write_mem), .Mem_Read(MEM_Read_mem), .Clk(clock_1_out), .Data_In(BUSB_mem),
    .Data_Out(main_10_data_out), .Alu_Result(Alu_res_mem));
  Multiplexer #(.width(32), .enable("false")) multiplexer_9 (
    .in0(Alu_res_mem), .in1(main_10_data_out), .out(mem_2prev), .sel(WB_mem));
  // Probe on rd_mem
  mem_wb_main main_11 (
    .reg_write(reg_write_mem), .rd_src(rd_src_mem), .PC_Plus_1(pc_plus_1_mem), .rd(rd_mem),
    .clk(clock_1_out), .out_11(reg_write_WB), .out_12(rd_src_WB), .out_13(PC_plus_1_WB), .out_14(rd_WB),
    .ALUres_or_DataOut(mem_2prev), .out_10(WB_3Prev), .imm16_16bit_mem(imm16_16bit_mem),
    .out_15(imm16_16bit_wb), .imm16_32_mem(imm16_32_mem), .out_16(imm16_32_wb), .BUSB_mem(BUSB_mem),
    .out_17(BUSB_wb));
  // Probe on rd_WB
  // Probe on WB_3Prev

  // Other names for the same wires on the sheet: RD_ID[4:0] = immd_L; imm16[8:5] = func_4bit;
  //   immd_U[10:0] = {imm16[15:9], func_4bit}; imm16_32_EX[15:0] = imm16_16bit_EX; R0[31:0] = out_1; R1[31:0] = out_2;
  //   R2[31:0] = out_3; R3[31:0] = out_4; R4[31:0] = out_5; R5[31:0] = out_6; R6[31:0] = out_7; R7[31:0] = out_8;
  //   R8[31:0] = out_9; R9[31:0] = out_10; R10[31:0] = out_11; R11[31:0] = out_12; R12[31:0] = out_13;
  //   R13[31:0] = out_14; R14[31:0] = out_15; R15[31:0] = out_16; R16[31:0] = out_17; R17[31:0] = out_18;
  //   R18[31:0] = out_19; R19[31:0] = out_20; R20[31:0] = out_21; R21[31:0] = out_22; R22[31:0] = out_23;
  //   R23[31:0] = out_24; R24[31:0] = out_25; R25[31:0] = out_26; R26[31:0] = out_27; R27[31:0] = out_28;
  //   R28[31:0] = out_29; R29[31:0] = out_30; R30[31:0] = out_31; R31[31:0] = out_32; rd_x[4:0] = rd_WB

  // Notes on the sheet:
  //   IF_ID
  //   op_code
  //   function
  //   ID_EX
  //   01-> SET
  //   0-> SSET
  //   10->ALU_Result
  //   EX_MEM
  //   MEM_WB
endmodule
