// Logisim project ex_mem.circ as structural Verilog: 2 circuits, main circuit main
module main (
  input  in_1,
  input  WB,
  input  MEM_Read,
  input  MEM_Write,
  input  Reg_write,
  input  [1:0] Rd_src,
  input  [19:0] PC_plus_1,
  input  [4:0] Rd,
  input  [31:0] Bus_B,
  input  [31:0] Alu_res,
  input  [15:0] imm16_16bit_EX,
  input  [31:0] imm16_32_EX,
  input  [31:0] BUSB_EX,
  output out_14,
  output out_15,
  output out_16,
  output out_17,
  output [1:0] out_18,
  output [19:0] out_19,
  output [4:0] out_20,
  output [31:0] out_21,
  output [31:0] out_22,
  output [15:0] out_23,
  output [31:0] out_24,
  output [31:0] out_25
);

  Register #(.width(1)) register_1 (.D(WB), .en(1'b1), .clk(in_1), .Q(out_14));  // open: clr
  Register #(.width(1)) register_2 (.D(MEM_Read), .en(1'b1), .clk(in_1), .Q(out_15));  // open: clr
  Register #(.width(1)) register_3 (.D(MEM_Write), .en(1'b1), .clk(in_1), .Q(out_16));  // open: clr
  Register #(.width(1)) register_4 (.D(Reg_write), .en(1'b1), .clk(in_1), .Q(out_17));  // open: clr
  Register #(.width(2)) register_5 (.D(Rd_src), .en(1'b1), .clk(in_1), .Q(out_18));  // open: clr
  Register #(.width(20)) register_6 (.D(PC_plus_1), .en(1'b1), .clk(in_1), .Q(out_19));  // open: clr
  Register #(.width(5)) register_7 (.D(Rd), .en(1'b1), .clk(in_1), .Q(out_20));  // open: clr
  Register #(.width(32)) register_8 (.D(Bus_B), .en(1'b1), .clk(in_1), .Q(out_21));  // open: clr
  Register #(.width(32)) register_9 (.D(Alu_res), .en(1'b1), .clk(in_1), .Q(out_22));  // open: clr
  Register #(.width(16)) register_10 (.D(imm16_16bit_EX), .en(1'b1), .clk(in_1), .Q(out_23));  // open: clr
  Register #(.width(32)) register_11 (.D(imm16_32_EX), .en(1'b1), .clk(in_1), .Q(out_24));  // open: clr
  Register #(.width(32)) register_12 (.D(BUSB_EX), .en(1'b1), .clk(in_1), .Q(out_25));  // open: clr

  // Other names for the same wires on the sheet: CLk = in_1

  // Notes on the sheet:
  //   WB
  //   Mem_read
  //   mem_Write
  //   reg_wreite
  //   Rd_src
  //   pc+1
  //   Rd
  //   bus B
  //   alu_res
endmodule

module block (
);

  main main_1 ();  // open: in_1, WB, MEM_Read, MEM_Write, Reg_write, Rd_src, PC_plus_1, Rd, Bus_B, Alu_res, out_14, out_15, out_16, out_17, out_18, out_19, out_20, out_21, out_22, imm16_16bit_EX, out_23, imm16_32_EX, out_24, BUSB_EX, out_25
endmodule
