// Logisim project if_id.circ as structural Verilog: 2 circuits, main circuit main
module main (
  input  [31:0] Instruction,
  input  [19:0] PC_plus_1,
  input  stall,
  input  in_4,
  output [31:0] out_5,
  output [19:0] out_6
);

  wire not_1_out;

  not not_1 (not_1_out, stall);
  Register #(.width(32)) register_1 (.D(Instruction), .en(not_1_out), .clk(in_4), .Q(out_5));  // open: clr
  Register #(.width(20)) register_2 (.D(PC_plus_1), .en(not_1_out), .clk(in_4), .Q(out_6));  // open: clr
endmodule

module block (
);

  main main_1 ();  // open: Instruction, PC_plus_1, out_5, out_6, in_4, stall
endmodule
