// Logisim project main_contr_unit.circ as structural Verilog
module main_control_unit (
  input  [5:0] opcode,
  output reg_write,
  output sset,
  output ext_op,
  output [1:0] Rd_src,
  output [1:0] alu_src,
  output mem_write,
  output mem_read,
  output wb
);

  wire and_1_out, and_2_out, and_4_out, and_5_out, and_6_out, and_7_out, and_8_out, and_9_out, and_10_out,
       and_13_out, and_14_out, and_15_out, not_1_out, not_2_out, not_3_out, not_4_out, not_5_out;
  wire [1:0] and_3_out;

  not not_1 (not_1_out, opcode[4]);
  not not_2 (not_2_out, opcode[3]);
  not not_3 (not_3_out, opcode[2]);
  not not_4 (not_4_out, opcode[1]);
  not not_5 (not_5_out, opcode[0]);
  and and_1 (and_1_out, opcode[4], opcode[1]);
  and and_2 (and_2_out, opcode[4], opcode[2]);
  and and_3 (and_3_out[0], opcode[3], opcode[2], opcode[1], opcode[0]);
  and and_4 (and_4_out, not_3_out, not_4_out, not_5_out);
  and and_5 (and_5_out, opcode[1], opcode[0]);
  and and_6 (and_6_out, not_3_out, opcode[0]);
  and and_7 (and_7_out, opcode[3], opcode[2], not_5_out);
  and and_8 (and_8_out, opcode[3], opcode[1]);
  and and_9 (and_9_out, not_4_out, not_5_out);
  and and_10 (and_10_out, opcode[1], opcode[0]);
  and and_11 (Rd_src[0], opcode[3], opcode[2], opcode[0]);
  and and_12 (alu_src[1], opcode[4], not_3_out, not_4_out, opcode[0]);
  and and_13 (and_13_out, not_1_out, not_2_out, not_3_out, not_4_out, not_5_out);
  and and_14 (and_14_out, opcode[4], opcode[1]);
  and and_15 (and_15_out, opcode[4], opcode[2]);
  and and_16 (mem_write, opcode[4], not_3_out, not_4_out, not_5_out);
  and and_17 (mem_read, opcode[4], not_3_out, not_4_out, opcode[0]);
  or or_1 (and_3_out[1], and_1_out, and_2_out);
  or or_2 (reg_write, not_1_out, and_4_out);
  or or_3 (ext_op, and_5_out, and_6_out, and_7_out, and_8_out);
  or or_4 (Rd_src[1], not_2_out, not_3_out, and_9_out, and_10_out);
  or or_5 (alu_src[0], and_13_out, and_14_out, and_15_out);

  assign sset = opcode[3];
  assign wb = opcode[4];
endmodule

module Main_Control_Block (
);

  main_control_unit main_control_unit_1 ();  // open: opcode, reg_write, sset, ext_op, Rd_src, alu_src, mem_write, mem_read, wb
endmodule
