// Logisim project mem_wb.circ as structural Verilog
module main (
  input  [31:0] Data_out,
  input  WB,
  input  reg_write,
  input  [1:0] rd_src,
  input  [19:0] PC_Plus_1,
  input  [4:0] rd,
  input  [31:0] alu_res,
  input  stall,
  input  clk,
  output [31:0] out_10,
  output out_11,
  output out_12,
  output [1:0] out_13,
  output [19:0] out_14,
  output [4:0] out_15,
  output [31:0] out_16
);

  wire not_1_out;

  not not_1 (not_1_out, stall);
  Register #(.width(32)) register_1 (.D(Data_out), .en(not_1_out), .clk(clk), .Q(out_10));  // open: clr
  Register #(.width(1)) register_2 (.D(WB), .en(not_1_out), .clk(clk), .Q(out_11));  // open: clr
  Register #(.width(1)) register_3 (.D(reg_write), .en(not_1_out), .clk(clk), .Q(out_12));  // open: clr
  Register #(.width(2)) register_4 (.D(rd_src), .en(not_1_out), .clk(clk), .Q(out_13));  // open: clr
  Register #(.width(20)) register_5 (.D(PC_Plus_1), .en(not_1_out), .clk(clk), .Q(out_14));  // open: clr
  Register #(.width(5)) register_6 (.D(rd), .en(not_1_out), .clk(clk), .Q(out_15));  // open: clr
  Register #(.width(32)) register_7 (.D(alu_res), .en(not_1_out), .clk(clk), .Q(out_16));  // open: clr

  // Notes on the sheet:
  //   WB
  //   reg_write
  //   rd_src
  //   PC_plus_1
  //   rd
endmodule
