// Logisim project pc_new.circ as structural Verilog: 2 circuits, main circuit main
module main (
  input  stall,
  input  Clk,
  input  [15:0] Imm16,
  input  [31:0] RS1,
  input  [1:0] Pc_Selctor,
  input  [10:0] Immu,
  input  [4:0] ImmL,
  input  [19:0] PC_ID,
  output [19:0] PC_Output,
  output [19:0] out_10
);

  wire not_1_out;
  wire [19:0] adder_3_out, bit_extender_2_out, multiplexer_1_out;
  wire [31:0] adder_2_out, bit_extender_1_out;

  Register #(.width(20)) PC_Count (.D(multiplexer_1_out), .en(not_1_out), .clk(Clk), .Q(PC_Output));  // open: clr
  not not_1 (not_1_out, stall);
  assign bit_extender_1_out = {{16{Imm16[15]}}, Imm16};  // Bit_Extender bit_extender_1
  assign bit_extender_2_out = {{4{Immu[10]}}, {Immu, ImmL}};  // Bit_Extender bit_extender_2
  Adder #(.width(20)) adder_1 (.a(PC_Output), .b(20'h1), .out(out_10));  // open: cin, cout
  Adder #(.width(32)) adder_2 (.a(bit_extender_1_out), .b(RS1), .out(adder_2_out));  // open: cin, cout
  Adder #(.width(20)) adder_3 (.a(PC_ID), .b(bit_extender_2_out), .out(adder_3_out));  // open: cin, cout
  Multiplexer #(.select(2), .width(20), .enable("false")) multiplexer_1 (
    .in0(out_10), .in1(adder_2_out[19:0]), .in2(adder_3_out), .out(multiplexer_1_out), .sel(Pc_Selctor));  // open: in3

  // Other names for the same wires on the sheet: pc[19:0] = PC_Output; pc_1[19:0] = out_10

  // Notes on the sheet:
  //   Next_PC
  //   Jump
  //   Branch
endmodule

module PC_BLOCK (
);

  main main_1 ();  // open: Pc_Selctor, Imm16, RS1, Immu, ImmL, PC_Output, Clk, out_10, stall, PC_ID
endmodule
